# Fritzing sketch Klingeltrafo_ESP32-C3-Mini-Breadboard (saved by Fritzing 1.0.4)
circuit board: 6.74697cm x 3.0659cm
stripboards: 1

parts:
  U1 = Sharp PC817 [package=THT]
  C4 = Electrolytic Capacitor [capacitance=47µF voltage=35V package="100 mil [THT, electrolytic]"]
  R2 = Resistor [tolerance=±5% resistance=3.3k power=0.25W package=THT]
  A1 = Esp32-c3 super mini
  R1 = Resistor [tolerance=±5% power=0.25W resistance=3.3k package=THT]
  D1 = Diode [package=diode-1n4148]
  J2 = Screw terminal - 2 pins [package=THT]

nets:
  N1: U1.Pin_1, R2.Pin_1, R1.Pin_1
  N2: U1.Pin_2, C4.-, J2.pin1
  N3: U1.Pin_4, A1.Pin_6
  N4: U1.Pin_3, A1.Pin_15
  N5: C4.+, R2.Pin_0, R1.Pin_0, D1.C
  N6: D1.A, J2.pin2

notes:
  GND
  3.3V
  GPIO
  ~8V/12V/24V
  Klingel (trafo)

custom parts:
  Esp32-c3 super mini: ESP32-C3 Development Board ESP32 SuperMini Development Board ESP32 Development Board WiFi Bluetooth.
